# Fritzing sketch volumeController (saved by Fritzing 0.9.3b)
breadboards: 1

parts:
  J1 = Piezo Speaker
  R3 = Rotary Potentiometer (Small) [maximum_resistance=100kΩ package=THT]
  Part1 = Arduino Uno (Rev3)

nets:
  N1: J1.pin1, R3.leg1, Part1.GND
  N2: J1.pin2, R3.wiper
  N3: R3.leg2, Part1.D13/SCK
